# Fritzing sketch schema (saved by Fritzing 0.9.0b)
breadboards: 1

parts:
  Arduino1 = Arduino Uno (Rev3)
  R1 = Photocell (LDR) [package=THT]
  R2 = Resistor [tolerance=±5% resistance=220 package=THT]
  R4 = Resistor [tolerance=±5% resistance=220 package=THT]
  R3 = Resistor [tolerance=±5% resistance=10k package=THT]
  R5 = Resistor [tolerance=±5% resistance=220 package=THT]
  R6 = Resistor [tolerance=±5% resistance=220 package=THT]
  R7 = Resistor [tolerance=±5% resistance=220 package=THT]
  R8 = Resistor [tolerance=±5% resistance=220 package=THT]
  LED7 = LED - 5mm [color="Red (633nm)" package="5 mm [THT]"]
  R9 = Resistor [tolerance=±5% resistance=220 package=THT]
  LED9 = LED - 5mm [color="Red (633nm)" package="5 mm [THT]"]
  LED10 = LED - 5mm [color="Red (633nm)" package="5 mm [THT]"]
  LED11 = LED - 5mm [color="Red (633nm)" package="5 mm [THT]"]
  LED12 = LED - 5mm [color="Red (633nm)" package="5 mm [THT]"]
  LED13 = LED - 5mm [color="Red (633nm)" package="5 mm [THT]"]
  LED14 = LED - 5mm [color="Red (633nm)" package="5 mm [THT]"]

nets:
  N1: Arduino1.A0, R1.pin_0, R3.Pin_1
  N2: Arduino1.D8, LED7.anode
  N3: Arduino1.D2, LED9.anode
  N4: Arduino1.D3_PWM, LED12.anode
  N5: Arduino1.D4, LED10.anode
  N6: Arduino1.D5_PWM, LED13.anode
  N7: Arduino1.D6_PWM, LED11.anode
  N8: Arduino1.D7, LED14.anode
  N9: Arduino1.5V, R1.pin_1, R3.Pin_0
  N10: Arduino1.GND, R2.Pin_0, R4.Pin_1, R5.Pin_0, R6.Pin_0, R7.Pin_1, R9.Pin_1
  N11: R2.Pin_1, LED9.cathode
  N12: R4.Pin_0, LED12.cathode
  N13: R5.Pin_1, LED10.cathode
  N14: R6.Pin_1, LED11.cathode
  N15: R7.Pin_0, LED13.cathode
  N16: R8.Pin_0, LED14.cathode
  N17: LED7.cathode, R9.Pin_0

notes:
  BLINK

// code stored in the sketch: Blink.ino
/*
  Blink
  
  Switching a LED on and off
  
  This example is part of the Fritzing Creator Kit: www.fritzing.org/creator-kit.
*/

int led = 13;                   // integer variable led is declared

void setup() {                  // the setup() method is executed only once
  pinMode(led, OUTPUT);         // the led PIN is declared as digital output
}

void loop() {                   // the loop() method is repeated
  digitalWrite(led, HIGH);      // switching on the led 
  delay(1000);                  // stopping the program for 1000 milliseconds
  digitalWrite(led, LOW);       // switching off the led 
  delay(1000);                  // stopping the program for 1000 milliseconds
}
